# Fritzing sketch Helicopter Prototype Circuit (saved by Fritzing 0.9.2b)
breadboards: 1

parts:
  Part1 = Arduino Uno (Rev3)
  R4 = Resistor [tolerance=±5% resistance=220 package=THT]
  R5 = Resistor [tolerance=±5% resistance=220 package=THT]
  R6 = Resistor [tolerance=±5% resistance=220 package=THT]
  LED1 = LED - 5mm [color="Red (633nm)" package="5 mm [THT]"]
  IC7 = IC, DIP package, 14 pins [chip_label=DAC]
  IC8 = IC, DIP package, 16 pins [chip_label=ADC]
  R7 = Resistor [tolerance=±5% resistance=220 package=THT]
  IC9 = IC, DIP package, 14 pins [chip_label="QUAD XOR"]
  IC10 = IC, DIP package, 14 pins [chip_label="QUAD OR"]
  R8 = Resistor [tolerance=±5% resistance=220 package=THT]
  C3 = Ceramic Capacitor [capacitance=10pF package="100 mil [THT, multilayer]"]
  C4 = Ceramic Capacitor [capacitance=100nF package="100 mil [THT, multilayer]"]

nets:
  N1: Part1.D9_PWM, IC8.pin2
  N2: Part1.D10_PWM/SS, IC7.pin3
  N3: Part1.D11_PWM/MOSI, IC7.pin5, IC8.pin3
  N4: Part1.D12/MISO, IC8.pin4
  N5: Part1.D13/SCK, IC7.pin4, IC8.pin5
  N6: Part1.D1/TX, R5.Pin_1
  N7: Part1.D6_PWM, LED1.cathode
  N8: R4.Pin_0, R6.Pin_1, IC7.pin8, IC7.pin12, IC8.pin1, IC8.pin6, IC9.pin14, IC10.pin14, C3.0, C4.0
  N9: R4.Pin_1, R5.Pin_0
  N10: R6.Pin_0, LED1.anode
  N11: IC7.pin1, IC7.pin9, IC7.pin11, IC7.pin13, IC8.pin7, IC8.pin8, IC9.pin7, IC10.pin7
  N12: R7.Pin_0, IC9.pin11, C3.1
  N13: R7.Pin_1, IC9.pin12
  N14: IC9.pin8, R8.Pin_0, C4.1
  N15: IC9.pin9, R8.Pin_1
  N16: IC9.pin10, IC10.pin8
  N17: IC9.pin13, IC10.pin9

notes:
  Y=In, G=Out, B=Misc.,O=DIn
  Relative to Breadboard:
